// Logisim project RAMSelect.circ as structural Verilog: 1 circuit, main circuit main
module main (
  input  in_1,
  input  in_2,
  input  in_3,
  input  in_4,
  input  in_5,
  input  in_6,
  input  in_7,
  input  in_8,
  input  in_9,
  input  in_10,
  input  DBIN,
  input  in_12,
  input  in_13,
  input  nWE,
  input  in_15,
  input  in_16,
  input  in_17,
  input  in_18,
  output nOE,
  output nS,
  output nW
);

  wire and_1_out, nand_1_out, not_1_out, not_2_out, not_3_out, or_1_out, or_2_out;

  not not_1 (not_1_out, in_16);
  not not_2 (not_2_out, in_17);
  not not_3 (not_3_out, in_18);
  or or_1 (or_1_out, in_12, in_10, in_9);
  or or_2 (or_2_out, in_9, in_10, in_12, in_13);
  nand nand_1 (nand_1_out, or_1_out, in_13);
  and and_1 (and_1_out, in_15, not_1_out, not_2_out, not_3_out);
  nand nand_2 (nS, or_2_out, nand_1_out, and_1_out);
  not not_4 (nOE, DBIN);

  assign nW = nWE;
endmodule
