// Logisim project RAMSelect_1.circ as structural Verilog: 1 circuit, main circuit main
module main (
  input  in_1,
  input  AD1,
  input  in_3,
  input  in_4,
  input  in_5,
  input  in_6,
  input  in_7,
  input  AD7,
  input  nWE,
  input  DBIN,
  input  AD8,
  input  AD9,
  input  AD10,
  input  AD11,
  input  in_15,
  input  in_16,
  input  in_17,
  input  in_18,
  output nW,
  output nOE,
  output nS
);

  wire nand_1_out, or_1_out, or_2_out;

  or or_1 (or_1_out, in_17, in_18);
  or or_2 (or_2_out, in_16, or_1_out);
  nand nand_1 (nand_1_out, or_2_out, or_2_out);
  // NAND_Gate nand_2 has open pins: in0=in_15, in1=nand_1_out, out=open
  nand nand_3 (nOE, DBIN, DBIN);

  assign nW = nWE;

  // Notes on the sheet:
  //   1000 ~ 1FFE
  //   0001 0000 0000 0000 ~ 0001 1111 1111 1110
endmodule
