// Logisim project INTREQ.circ as structural Verilog: 1 circuit, main circuit main
module main (
  input  DR,
  input  INT_FIN_MMIO,
  input  IR2,
  input  IR3,
  input  IR4,
  input  IR5,
  input  IR6,
  input  IR7,
  input  IR8,
  output nIRQ
);

  wire and_1_out, and_2_out, and_3_out, and_4_out, and_5_out, and_6_out, and_7_out, and_8_out, clock_1_out,
       d_ff_1_q, d_ff_2_q, d_ff_3_q, d_ff_4_q, d_ff_5_q, d_ff_6_q, d_ff_7_q, d_ff_8_q, or_1_out, or_2_out,
       or_3_out, or_4_out, or_5_out, or_6_out, or_7_out;

  Clock clock_1 (.out(clock_1_out));
  and and_1 (and_1_out, DR, nIRQ);
  and and_2 (and_2_out, IR2, nIRQ);
  and and_3 (and_3_out, IR3, nIRQ);
  and and_4 (and_4_out, IR4, nIRQ);
  and and_5 (and_5_out, IR5, nIRQ);
  and and_6 (and_6_out, IR6, nIRQ);
  and and_7 (and_7_out, IR7, nIRQ);
  and and_8 (and_8_out, IR8, nIRQ);
  D_Flip_Flop d_ff_1 (.clk(clock_1_out), .D(and_1_out), .Q(d_ff_1_q), .reset(INT_FIN_MMIO));  // open: Qn, preset, en
  or or_1 (or_1_out, d_ff_1_q, d_ff_2_q);
  D_Flip_Flop d_ff_2 (.clk(clock_1_out), .D(and_2_out), .Q(d_ff_2_q), .reset(INT_FIN_MMIO));  // open: Qn, preset, en
  D_Flip_Flop d_ff_3 (.clk(clock_1_out), .D(and_3_out), .Q(d_ff_3_q), .reset(INT_FIN_MMIO));  // open: Qn, preset, en
  or or_2 (or_2_out, d_ff_3_q, d_ff_4_q);
  D_Flip_Flop d_ff_4 (.clk(clock_1_out), .D(and_4_out), .Q(d_ff_4_q), .reset(INT_FIN_MMIO));  // open: Qn, preset, en
  D_Flip_Flop d_ff_5 (.clk(clock_1_out), .D(and_5_out), .Q(d_ff_5_q), .reset(INT_FIN_MMIO));  // open: Qn, preset, en
  or or_3 (or_3_out, d_ff_5_q, d_ff_6_q);
  D_Flip_Flop d_ff_6 (.clk(clock_1_out), .D(and_6_out), .Q(d_ff_6_q), .reset(INT_FIN_MMIO));  // open: Qn, preset, en
  D_Flip_Flop d_ff_7 (.clk(clock_1_out), .D(and_7_out), .Q(d_ff_7_q), .reset(INT_FIN_MMIO));  // open: Qn, preset, en
  or or_4 (or_4_out, d_ff_7_q, d_ff_8_q);
  D_Flip_Flop d_ff_8 (.clk(clock_1_out), .D(and_8_out), .Q(d_ff_8_q), .reset(INT_FIN_MMIO));  // open: Qn, preset, en
  or or_5 (or_5_out, or_1_out, or_2_out);
  or or_6 (or_6_out, or_3_out, or_4_out);
  or or_7 (or_7_out, or_5_out, or_6_out);
  not not_1 (nIRQ, or_7_out);
endmodule
