// Logisim project MMIO.circ as structural Verilog: 1 circuit, main circuit main
module main (
  input  AD1,
  input  AD2,
  input  AD3,
  input  AD4,
  input  AD5,
  input  AD6,
  input  AD7,
  input  AD8,
  input  AD9,
  input  AD10,
  input  AD11,
  input  AD12,
  input  AD13,
  input  AD14,
  input  AD15
);

  wire [6:3] or_1_out;
  wire [7:0] rom_1_data;

  or or_1 (or_1_out[3], AD4, AD5);
  or or_2 (or_1_out[4], AD6, AD7);
  or or_3 (or_1_out[5], AD8, AD9);
  or or_4 (or_1_out[6], AD10, AD11);
  ROM #(.addrWidth(11)) rom_1 (
    .addr({AD15, AD14, AD13, AD12, or_1_out, AD3, AD2, AD1}), .data(rom_1_data));  // open: sel

  // Notes on the sheet:
  //   contents of rom_1 (hex, n*v repeats v):
  //   256*0 1 2 3
endmodule
