// Logisim project MUX_MMIO.circ as structural Verilog: 1 circuit, main circuit main
module main (
  input  A12,
  input  A13,
  input  A14,
  input  A15
);

  wire nand_1_out, nand_2_out, or_1_out;

  nand nand_1 (nand_1_out, A12, A13);
  or or_1 (or_1_out, nand_1_out, nand_2_out);
  nand nand_2 (nand_2_out, A14, A15);
  LED QCE (.in(or_1_out));
endmodule
