// Logisim project RAM_DMA.circ as structural Verilog: 1 circuit, main circuit main
module main (
  input  A12,
  input  A12_2,
  input  A13,
  input  A13_2,
  input  A14,
  input  A14_2,
  input  A15,
  input  A15_2,
  input  nDMAW,
  input  HOLDA,
  input  nDMAR,
  input  nMEMEN,
  input  DBIN,
  input  nWE,
  output nCS,
  output nCS_2,
  output nWE_2,
  output CS2,
  output nOE,
  output nCS1
);

  wire nand_1_out, nand_2_out, nand_3_out, nand_4_out, nand_6_out, nand_8_out, not_1_out, not_2_out,
       not_3_out, or_1_out, or_3_out, or_4_out;

  not not_1 (not_1_out, A13);
  or or_1 (or_1_out, not_1_out, A14);
  Pull_Resistor #(.pull(1)) pull_resistor_1 (.node(DBIN));
  Pull_Resistor #(.pull(1)) pull_resistor_2 (.node(nWE));
  Pull_Resistor #(.pull(1)) pull_resistor_3 (.node(nMEMEN));
  or or_2 (nCS1, or_1_out, A15);
  nand nand_1 (nand_1_out, HOLDA, HOLDA);
  or or_3 (or_3_out, nMEMEN, not_2_out);
  not not_2 (not_2_out, DBIN);
  or or_4 (or_4_out, nMEMEN, nWE);
  nand nand_2 (nand_2_out, nDMAR, HOLDA);
  nand nand_3 (nand_3_out, nand_1_out, or_3_out);
  nand nand_4 (nand_4_out, HOLDA, HOLDA);
  nand nand_5 (nOE, nand_2_out, nand_3_out);
  nand nand_6 (nand_6_out, nDMAW, HOLDA);
  nand nand_7 (nWE_2, nand_6_out, nand_8_out);
  nand nand_8 (nand_8_out, nand_4_out, or_4_out);
  not not_3 (not_3_out, A14_2);
  or or_5 (nCS, not_3_out, A15_2);

  assign CS2 = 1'b1;
  assign nCS_2 = nCS1;

  // Notes on the sheet:
  //   0010 ~ 0011
  //   0100 ~ 0111
endmodule
