// Logisim project RAM_ROM_Select.circ as structural Verilog: 1 circuit, main circuit main
module main (
  input  AD1,
  input  AD2,
  input  AD3,
  input  AD4,
  input  AD5,
  input  AD6,
  input  AD7,
  input  AD8,
  input  AD9,
  input  AD10,
  input  AD11,
  input  AD12,
  input  AD13,
  input  AD14,
  input  AD15,
  input  nMEMEN,
  input  DBIN,
  input  nWE,
  output nOE__ROM,
  output nOE__LOCAL_RAM,
  output nS__LOCAL_RAM,
  output nW__LOCAL_RAM
);

  wire nand_1_out, not_1_out, or_1_out, or_2_out, or_3_out, or_4_out, or_5_out, or_6_out;

  not not_1 (not_1_out, nMEMEN);
  not not_2 (nW__LOCAL_RAM, nWE);
  not not_3 (nOE__LOCAL_RAM, DBIN);
  or or_1 (or_1_out, AD12, AD13);
  or or_2 (or_2_out, AD14, AD15);
  or or_3 (or_3_out, not_1_out, nOE__LOCAL_RAM);
  or or_4 (or_4_out, AD13, or_5_out);
  or or_5 (or_5_out, AD14, AD15);
  or or_6 (or_6_out, or_1_out, or_2_out);
  or or_7 (nOE__ROM, or_6_out, or_3_out);
  nand nand_1 (nand_1_out, or_4_out, or_4_out);
  nand nand_2 (nS__LOCAL_RAM, AD12, nand_1_out);

  // Notes on the sheet:
  //   FFFC ~ FFFE: LOAD SIGNAL VECTOR
  //   0000 ~ 0FFE: CONSOLE ROM (2K WORDS / 4K BYTES)
  //   1000 ~ 1FFE: LOCAL REGISTER RAM (2K WORDS / 4K BYTES)
  //   2000 ~ FEFE: GENERAL PURPOSE RAM (28K WORDS / 56K BYTES)
  //   FF00 ~ FFFA: MMIO ADDRESS SPACE (126 WORDS / 252 BYTES)
endmodule
