// Logisim project RAM_Select.circ as structural Verilog: 1 circuit, main circuit main
module main (
  input  AD12,
  input  AD13,
  input  AD14,
  input  AD15,
  input  nMEMEN,
  input  DBIN,
  input  nWE,
  output nCS__RAM1,
  output nCS__RAM2,
  output nCS__RAM3,
  output nW__RAM
);

  wire nand_1_out, nand_2_out, nand_3_out, or_1_out, or_2_out, or_3_out, or_4_out;

  nand nand_1 (nand_1_out, AD12, AD12);
  or or_1 (or_1_out, nand_1_out, AD13);
  nand nand_2 (nand_2_out, AD13, AD13);
  or or_2 (or_2_out, nand_2_out, AD12);
  nand nand_3 (nand_3_out, AD13, AD12);
  or or_3 (or_3_out, AD14, AD15);
  or or_4 (or_4_out, or_3_out, nMEMEN);
  or or_5 (nCS__RAM1, or_1_out, or_4_out);
  or or_6 (nCS__RAM2, or_2_out, or_4_out);
  or or_7 (nCS__RAM3, nand_3_out, or_4_out);
  // NAND_Gate nand_4 is placed but not wired
  // OR_Gate or_8 is placed but not wired

  assign nW__RAM = nWE;

  // Notes on the sheet:
  //   0000 ~ 0FFE: CONSOLE ROM (2K WORDS / 4K BYTES)
  //   1000 ~ 3FFE: FAST SRAM (6K WORDS / 12K BYTES)
  //   4000 ~ FBFE: EXTENDED RAM (23K WORDS / 46K BYTES)
  //   FFFC ~ FFFE: LOAD SIGNAL VECTOR
  //   FC00 ~ FFFA: MMIO ADDRESS SPACE (1K WORDS / 2K BYTES)
  //   0001 0000 0000 0000 - 0001 1111 1111 1110
  //   0010 0000 0000 0000 - 0010 1111 1111 1110
  //   0011 0000 0000 0000 - 0011 1111 1111 1110
endmodule
