// Logisim project ROM_Select.circ as structural Verilog: 1 circuit, main circuit main
module main (
  input  AD12,
  input  AD13,
  input  AD14,
  input  AD15,
  input  nMEMEN,
  input  DBIN,
  output nOE__ROM
);

  wire nand_1_out, nand_2_out, nand_3_out, or_1_out, or_2_out, or_3_out, or_4_out;

  or or_1 (or_1_out, AD12, AD13);
  or or_2 (or_2_out, or_1_out, or_3_out);
  or or_3 (or_3_out, AD14, AD15);
  nand nand_1 (nand_1_out, DBIN, DBIN);
  or or_4 (or_4_out, nand_1_out, nMEMEN);
  nand nand_2 (nand_2_out, or_2_out, or_2_out);
  nand nand_3 (nand_3_out, or_4_out, or_4_out);
  nand nand_4 (nOE__ROM, nand_2_out, nand_3_out);

  // Notes on the sheet:
  //   FFFC ~ FFFE: LOAD SIGNAL VECTOR
  //   0000 ~ 0FFE: CONSOLE ROM (2K WORDS / 4K BYTES)
  //   1000 ~ 1FFE: LOCAL REGISTER RAM (2K WORDS / 4K BYTES)
  //   2000 ~ FEFE: GENERAL PURPOSE RAM (28K WORDS / 56K BYTES)
  //   FF00 ~ FFFA: MMIO ADDRESS SPACE (126 WORDS / 252 BYTES)
endmodule
